# Fritzing sketch cubebot (saved by Fritzing 0.7.10b)
breadboards: 1

parts:
  Arduino1 = Arduino
  J1 = Basic Servo
  J2 = Basic Servo
  R1 = Resistor [tolerance=±5% resistance=220 package=THT]
  R2 = Resistor [tolerance=±5% resistance=220 package=THT]
  R3 = Resistor [tolerance=±5% resistance=220 package=THT]
  R4 = Resistor [tolerance=±5% resistance=220 package=THT]
  S1 = Toggle Switch [package=THT]
  S2 = Toggle Switch [package=THT]
  S3 = Toggle Switch [package=THT]
  LED1 = LED - 5mm [color="Red (633nm)" package="5 mm [THT]"]
  LED2 = LED - 5mm [color="Red (633nm)" package="5 mm [THT]"]

nets:
  N1: Arduino1.D10, R3.Pin_1, S3.L2
  N2: Arduino1.D9, R4.Pin_1, S2.L2
  N3: Arduino1.D8, R2.Pin_1, S1.L2
  N4: Arduino1.D7, J2.pulse
  N5: Arduino1.D6, J1.pulse
  VCC: Arduino1.+5V, J1.vcc, J2.vcc, S2.COM, S3.COM, LED1.anode, LED2.anode
  GND: Arduino1.GND, J1.gnd, J2.gnd, R1.Pin_0, R2.Pin_0, R3.Pin_0, R4.Pin_0
  N6: R1.Pin_1, LED1.cathode, LED2.cathode
